// Logisim project computer.circ as structural Verilog: 7 circuits, main circuit main
module main (
);

  wire \alu_1_溢出信号 , \alu_1_结果为0信号 , \alu_1_结果为负信号 , CLK, \controller_1_alu减法 , \controller_1_ram写使能 ,
       \controller_1_ram读使能 , \controller_1_使能a寄存器 , \controller_1_使能b寄存器 , \controller_1_使能c寄存器 ,
       \controller_1_使能d寄存器 , \controller_1_节拍0 , \controller_1_节拍1 , \controller_1_节拍2 , \controller_1_节拍3 ,
       \controller_1_节拍4 , \controller_1_节拍5 , RST;
  wire [7:0] \alu_1_输出信号 , \controller_1_alu操作数a , \controller_1_alu操作数b , controller_1_ir, controller_1_pc,
       \controller_1_ram地址总线 , ram_1_data, \寄存器_A_q , \寄存器_B_q , \寄存器_C_q , \寄存器_D_q ;

  // Probe on \controller_1_alu减法 
  // Probe on \controller_1_alu操作数a 
  ALU alu_1 (
    .\操作数A (\controller_1_alu操作数a ), .\操作数B (\controller_1_alu操作数b ), .\减法 (\controller_1_alu减法 ),
    .\溢出信号 (\alu_1_溢出信号 ), .\输出信号 (\alu_1_输出信号 ), .\结果为0信号 (\alu_1_结果为0信号 ), .\结果为负信号 (\alu_1_结果为负信号 ));
  // Probe on \controller_1_alu操作数b 
  // Probe on \alu_1_输出信号 
  Clock \u_时钟信号  (.out(CLK));
  Register \u_寄存器_A  (.D(ram_1_data), .en(\controller_1_使能a寄存器 ), .Q(\寄存器_A_q ), .clk(CLK), .clr(RST));
  Button \u_复位  (.out(RST));
  Controller controller_1 (
    .\时钟 (CLK), .\复位 (RST), .\RAM数据总线 (ram_1_data), .\RAM地址总线 (\controller_1_ram地址总线 ),
    .\使能A寄存器 (\controller_1_使能a寄存器 ), .\使能B寄存器 (\controller_1_使能b寄存器 ), .\使能C寄存器 (\controller_1_使能c寄存器 ),
    .\使能D寄存器 (\controller_1_使能d寄存器 ), .\ALU操作数A (\controller_1_alu操作数a ), .\ALU操作数B (\controller_1_alu操作数b ),
    .\ALU溢出 (\alu_1_溢出信号 ), .\ALU为0 (\alu_1_结果为0信号 ), .\ALU为负 (\alu_1_结果为负信号 ), .\节拍0 (\controller_1_节拍0 ),
    .\节拍1 (\controller_1_节拍1 ), .\节拍2 (\controller_1_节拍2 ), .\节拍3 (\controller_1_节拍3 ),
    .\节拍4 (\controller_1_节拍4 ), .\节拍5 (\controller_1_节拍5 ), .PC(controller_1_pc), .IR(controller_1_ir),
    .\ALU减法 (\controller_1_alu减法 ), .\ALU结果 (\alu_1_输出信号 ), .\寄存器A (\寄存器_A_q ), .\寄存器B (\寄存器_B_q ),
    .\寄存器C (\寄存器_C_q ), .\寄存器D (\寄存器_D_q ), .\RAM读使能 (\controller_1_ram读使能 ), .\RAM写使能 (\controller_1_ram写使能 ));
  Register \u_寄存器_B  (.D(ram_1_data), .en(\controller_1_使能b寄存器 ), .Q(\寄存器_B_q ), .clk(CLK), .clr(RST));
  Register \u_寄存器_C  (.D(ram_1_data), .en(\controller_1_使能c寄存器 ), .Q(\寄存器_C_q ), .clk(CLK), .clr(RST));
  LED led_1 (.in(\controller_1_节拍0 ));
  LED led_2 (.in(\controller_1_节拍1 ));
  LED led_3 (.in(\controller_1_节拍2 ));
  LED led_4 (.in(\controller_1_节拍3 ));
  Register \u_寄存器_D  (.D(ram_1_data), .en(\controller_1_使能d寄存器 ), .Q(\寄存器_D_q ), .clk(CLK), .clr(RST));
  LED led_5 (.in(\controller_1_节拍5 ));
  LED led_6 (.in(\controller_1_节拍4 ));
  // Probe on controller_1_ir
  // Probe on controller_1_pc
  // Probe on ram_1_data
  // Probe on \controller_1_ram地址总线 
  RAM #(.bus("separate")) ram_1 (
    .addr(\controller_1_ram地址总线 ), .din(ram_1_data), .data(ram_1_data), .str(\controller_1_ram写使能 ),
    .clk(CLK), .ld(\controller_1_ram读使能 ));  // open: sel, clr

  // Notes on the sheet:
  //   随机访问存储器（RAM）
  //   在简易计算机中存放指令和数据
endmodule

module Controller (
  input  \时钟 ,
  input  \复位 ,
  input  [7:0] \RAM数据总线 ,
  input  [7:0] \ALU结果 ,
  input  \ALU溢出 ,
  input  \ALU为负 ,
  input  \ALU为0 ,
  input  [7:0] \寄存器A ,
  input  [7:0] \寄存器B ,
  input  [7:0] \寄存器C ,
  input  [7:0] \寄存器D ,
  output \节拍0 ,
  output [7:0] PC,
  output \节拍1 ,
  output \节拍2 ,
  output \节拍3 ,
  output [7:0] IR,
  output \节拍4 ,
  output \节拍5 ,
  output [7:0] \RAM地址总线 ,
  output \RAM读使能 ,
  output \RAM写使能 ,
  output \使能A寄存器 ,
  output \使能B寄存器 ,
  output \使能C寄存器 ,
  output \使能D寄存器 ,
  output [7:0] \ALU操作数A ,
  output [7:0] \ALU操作数B ,
  output \ALU减法 
);

  wire ADD, ALU_SUB, FR_EN, HALT, IR_EN, IS_CALC, IS_JMP, IS_LD, IS_STO, JMP, JNZ, JZ, LDA, LDB, LDC, LDD,
       PC_EN, PC_LD, RAM_A_MUX, STOA, STOB, STOC;
  wire [1:0] ALU_A_MUX, ALU_B_MUX;
  wire [7:0] FR, PC_IN;
  wire [7:3] FR_IN;

  Multiplexer #(.select(2), .width(8), .enable("false")) multiplexer_1 (
    .in0(\寄存器A ), .in1(\寄存器B ), .in2(\寄存器C ), .in3(\寄存器D ), .out(\ALU操作数A ), .sel(ALU_A_MUX));
  Multiplexer #(.select(2), .width(8), .enable("false")) multiplexer_2 (
    .in0(\寄存器A ), .in1(\寄存器B ), .in2(\寄存器C ), .in3(\寄存器D ), .out(\ALU操作数B ), .sel(ALU_B_MUX));
  Register \u_指令寄存器_IR  (.D(\RAM数据总线 ), .en(IR_EN), .Q(IR), .clk(\时钟 ), .clr(\复位 ));
  Counter \u_程序计数器_PC  (.load(PC_LD), .D(PC_IN), .count(PC_EN), .Q(PC), .clk(\时钟 ), .clr(\复位 ));  // open: carry
  Register \u_标志寄存器_FR  (.D({FR_IN, \ALU为0 , \ALU为负 , \ALU溢出 }), .en(FR_EN), .Q(FR), .clk(\时钟 ), .clr(\复位 ));
  // Probe on PC_IN
  assign PC_IN = {{4{1'b0}}, IR[3:0]};  // Bit_Extender bit_extender_1
  Multiplexer #(.width(8), .enable("false")) multiplexer_3 (.in0(PC), .in1(PC_IN), .out(\RAM地址总线 ), .sel(RAM_A_MUX));
  // Probe on RAM_A_MUX
  Loop_Counter loop_counter_1 (
    .CLK(\时钟 ), .RST(\复位 ), .T0(\节拍0 ), .T1(\节拍1 ), .T2(\节拍2 ), .T3(\节拍3 ), .T4(\节拍4 ), .T5(\节拍5 ));
  Instruction_Decoder instruction_decoder_1 (
    .IR(IR), .LDA(LDA), .LDB(LDB), .LDC(LDC), .LDD(LDD), .ADD(ADD), .SUB(\ALU减法 ), .STOA(STOA), .STOB(STOB),
    .STOC(STOC), .STOD(STOB), .JMP(JMP), .JZ(JZ), .JNZ(JNZ), .HALT(HALT));
  or or_1 (IS_LD, LDA, LDB, LDC, LDD);
  or or_2 (IS_CALC, ADD, \ALU减法 );
  or or_3 (IS_STO, STOA, STOB, STOC, STOB);
  or or_4 (IS_JMP, JMP, JZ, JNZ);
  Control_Matrix control_matrix_1 (
    .T0(\节拍0 ), .T1(\节拍1 ), .T2(\节拍2 ), .T3(\节拍3 ), .T4(\节拍4 ), .T5(\节拍5 ), .LDA(LDA), .LDB(LDB), .LDC(LDC),
    .LDD(LDD), .ADD(ADD), .SUB(\ALU减法 ), .STOA(STOA), .STOB(STOB), .STOC(STOC), .STOD(STOB), .JMP(JMP),
    .JZ(JZ), .JNZ(JNZ), .HALT(HALT), .IS_LD(IS_LD), .IS_CALC(IS_CALC), .IS_STO(IS_STO), .IS_JMP(IS_JMP),
    .IR(IR), .FR(FR), .IR_EN(IR_EN), .PC_EN(PC_EN), .RAM_A_MUX(RAM_A_MUX), .RAM_RE(\RAM读使能 ),
    .RAM_WE(\RAM写使能 ), .REG_A_EN(\使能A寄存器 ), .REG_B_EN(\使能B寄存器 ), .REG_C_EN(\使能C寄存器 ), .REG_D_EN(\使能D寄存器 ),
    .ALU_A_MUX(ALU_A_MUX), .ALU_B_MUX(ALU_B_MUX), .ALU_SUB(ALU_SUB), .PC_LD(PC_LD), .FR_EN(FR_EN));

  // Other names for the same wires on the sheet: ALU_A[7:0] = \ALU操作数A ; ALU_B[7:0] = \ALU操作数B ; ALU_S[7:0] = \ALU结果 ;
  //   CLK = \时钟 ; ALU_O = \ALU溢出 ; FR_IN[2:0] = {\ALU为0 , \ALU为负 , \ALU溢出 }; ALU_N = \ALU为负 ; ALU_Z = \ALU为0 ;
  //   RAM_A[7:0] = \RAM地址总线 ; RAM_D[7:0] = \RAM数据总线 ; RAM_RD = \RAM读使能 ; RAM_WR = \RAM写使能 ; REG_A[7:0] = \寄存器A ;
  //   REG_A_EN = \使能A寄存器 ; REG_B[7:0] = \寄存器B ; REG_B_EN = \使能B寄存器 ; REG_C[7:0] = \寄存器C ; REG_C_EN = \使能C寄存器 ;
  //   REG_D[7:0] = \寄存器D ; REG_D_EN = \使能D寄存器 ; RST = \复位 ; SUB = \ALU减法 ; T0 = \节拍0 ; T1 = \节拍1 ; T2 = \节拍2 ;
  //   T3 = \节拍3 ; T4 = \节拍4 ; T5 = \节拍5 

  // Notes on the sheet:
  //   ALU复用器组
  //   把输入端复用给不同寄存器
  //   环形计数器
  //   是LOAD指令
  //   是计算指令
  //   译码部分
  //   是STO指令
endmodule

module Control_Matrix (
  input  T0,
  input  T1,
  input  T2,
  input  T3,
  input  T4,
  input  T5,
  input  LDA,
  input  LDB,
  input  LDC,
  input  LDD,
  input  ADD,
  input  SUB,
  input  STOA,
  input  STOB,
  input  STOC,
  input  STOD,
  input  JMP,
  input  JZ,
  input  JNZ,
  input  HALT,
  input  IS_LD,
  input  IS_CALC,
  input  IS_STO,
  input  IS_JMP,
  input  [7:0] IR,
  input  [7:0] FR,
  output IR_EN,
  output PC_EN,
  output RAM_A_MUX,
  output RAM_RE,
  output RAM_WE,
  output REG_A_EN,
  output REG_B_EN,
  output REG_C_EN,
  output REG_D_EN,
  output [1:0] ALU_A_MUX,
  output [1:0] ALU_B_MUX,
  output ALU_SUB,
  output PC_LD,
  output FR_EN
);

  wire and_1_out, and_2_out, and_3_out, and_4_out, and_10_out, and_11_out, and_12_out, and_13_out,
       and_14_out, not_1_out, or_3_out;

  and and_1 (and_1_out, T4, IS_LD);
  and and_2 (and_2_out, T3, IS_LD);
  or or_1 (RAM_A_MUX, and_2_out, and_1_out, and_3_out);
  and and_3 (and_3_out, T5, IS_LD);
  or or_2 (RAM_RE, T0, and_4_out);
  and and_4 (and_4_out, T5, IS_LD);
  and and_5 (RAM_WE, T3, IS_STO);
  and and_6 (REG_A_EN, T4, LDA);
  and and_7 (REG_B_EN, T4, LDB);
  and and_8 (REG_C_EN, T4, LDC);
  and and_9 (REG_D_EN, T4, LDD);
  assign ALU_A_MUX = or_3_out ? IR[3:2] : 2'bz;  // Controlled_Buffer controlled_buffer_1
  and and_10 (and_10_out, T4, IS_CALC);
  and and_11 (and_11_out, T3, IS_CALC);
  or or_3 (or_3_out, and_11_out, and_10_out);
  assign ALU_B_MUX = or_3_out ? IR[1:0] : 2'bz;  // Controlled_Buffer controlled_buffer_2
  and and_12 (and_12_out, T4, JMP);
  and and_13 (and_13_out, T4, JZ, FR[2]);
  or or_4 (PC_LD, and_12_out, and_13_out, and_14_out);
  not not_1 (not_1_out, FR[2]);
  and and_14 (and_14_out, T4, JNZ, not_1_out);
  and and_15 (FR_EN, T4, IS_CALC);

  assign ALU_SUB = SUB;
  assign IR_EN = T1;
  assign PC_EN = T2;
endmodule

module ALU (
  input  [7:0] \操作数A ,
  input  [7:0] \操作数B ,
  input  \减法 ,
  output \溢出信号 ,
  output [7:0] \输出信号 ,
  output \结果为0信号 ,
  output \结果为负信号 
);

  wire [7:0] adder_1_out, subtractor_1_out;

  Adder adder_1 (.a(\操作数A ), .b(\操作数B ), .out(adder_1_out), .cout(\溢出信号 ));  // open: cin
  Subtractor subtractor_1 (.a(\操作数A ), .b(\操作数B ), .out(subtractor_1_out), .bout(\结果为负信号 ));  // open: bin
  Multiplexer #(.width(8), .enable("false")) multiplexer_1 (
    .in0(adder_1_out), .in1(subtractor_1_out), .out(\输出信号 ), .sel(\减法 ));
  nor nor_1 (\结果为0信号 , \输出信号 [0], \输出信号 [1], \输出信号 [2], \输出信号 [3], \输出信号 [4], \输出信号 [5], \输出信号 [6], \输出信号 [7]);

  // Other names for the same wires on the sheet: SUBTRACT = \减法 
endmodule

module Instruction_Decoder (
  input  [7:0] IR,
  output LDA,
  output LDB,
  output LDC,
  output LDD,
  output ADD,
  output SUB,
  output STOA,
  output STOB,
  output STOC,
  output STOD,
  output JMP,
  output JZ,
  output JNZ,
  output HALT
);

  wire not_1_out, not_2_out, not_3_out, not_4_out, not_5_out, not_6_out, not_7_out, not_8_out, not_9_out,
       not_10_out, not_11_out, not_12_out, not_13_out, not_14_out, not_15_out, not_16_out, not_17_out,
       not_18_out, not_19_out, not_20_out, not_21_out, not_22_out, not_23_out, not_24_out, not_25_out,
       not_26_out, not_27_out, not_28_out;

  not not_1 (not_1_out, IR[7]);
  not not_2 (not_2_out, IR[6]);
  not not_3 (not_3_out, IR[5]);
  not not_4 (not_4_out, IR[7]);
  not not_5 (not_5_out, IR[6]);
  not not_6 (not_6_out, IR[4]);
  not not_7 (not_7_out, IR[7]);
  not not_8 (not_8_out, IR[6]);
  not not_9 (not_9_out, IR[7]);
  not not_10 (not_10_out, IR[5]);
  not not_11 (not_11_out, IR[4]);
  not not_12 (not_12_out, IR[7]);
  not not_13 (not_13_out, IR[5]);
  not not_14 (not_14_out, IR[7]);
  not not_15 (not_15_out, IR[4]);
  not not_16 (not_16_out, IR[7]);
  not not_17 (not_17_out, IR[6]);
  not not_18 (not_18_out, IR[5]);
  not not_19 (not_19_out, IR[4]);
  not not_20 (not_20_out, IR[6]);
  not not_21 (not_21_out, IR[5]);
  not not_22 (not_22_out, IR[6]);
  not not_23 (not_23_out, IR[4]);
  not not_24 (not_24_out, IR[6]);
  not not_25 (not_25_out, IR[5]);
  not not_26 (not_26_out, IR[4]);
  not not_27 (not_27_out, IR[5]);
  not not_28 (not_28_out, IR[4]);
  and and_1 (LDA, not_1_out, not_2_out, not_3_out, IR[4]);
  and and_2 (LDB, not_4_out, not_5_out, IR[5], not_6_out);
  and and_3 (LDC, not_7_out, not_8_out, IR[5], IR[4]);
  and and_4 (LDD, not_9_out, IR[6], not_10_out, not_11_out);
  and and_5 (ADD, not_12_out, IR[6], not_13_out, IR[4]);
  and and_6 (SUB, not_14_out, IR[6], IR[5], not_15_out);
  and and_7 (STOA, not_16_out, IR[6], IR[5], IR[4]);
  and and_8 (STOB, IR[7], not_17_out, not_18_out, not_19_out);
  and and_9 (STOC, IR[7], not_20_out, not_21_out, IR[4]);
  and and_10 (STOD, IR[7], not_22_out, IR[5], not_23_out);
  and and_11 (JMP, IR[7], not_24_out, IR[5], IR[4]);
  and and_12 (JZ, IR[7], IR[6], not_25_out, not_26_out);
  and and_13 (JNZ, IR[7], IR[6], not_27_out, IR[4]);
  and and_14 (HALT, IR[7], IR[6], IR[5], not_28_out);

  // Notes on the sheet:
  //   译码器 用途：解读从指令寄存器（IR）来的指令的头四位
endmodule

module Loop_Counter (
  input  CLK,
  input  RST,
  output T0,
  output T1,
  output T2,
  output T3,
  output T4,
  output T5
);

  D_Flip_Flop d_ff_1 (.clk(CLK), .D(T5), .Q(T0), .preset(RST));  // open: Qn, en, reset
  D_Flip_Flop d_ff_2 (.clk(CLK), .D(T0), .Q(T1), .reset(RST));  // open: Qn, preset, en
  D_Flip_Flop d_ff_3 (.clk(CLK), .D(T1), .Q(T2), .reset(RST));  // open: Qn, preset, en
  D_Flip_Flop d_ff_4 (.clk(CLK), .D(T2), .Q(T3), .reset(RST));  // open: Qn, preset, en
  D_Flip_Flop d_ff_5 (.clk(CLK), .D(T3), .Q(T4), .reset(RST));  // open: Qn, preset, en
  D_Flip_Flop d_ff_6 (.clk(CLK), .D(T4), .Q(T5), .reset(RST));  // open: Qn, preset, en

  // Notes on the sheet:
  //   复位后默认第一个D触发器为高电平
  //   环形计数器  用途：依次使T0~T6为1，让计算机在一个时钟周期里完成取指令、执行指令的操作
endmodule

module _8_bit_transmission_gate (
  input  B__A,
  input  [7:0] A,
  input  [7:0] B,
  input  A__B
);

  assign A = B__A ? B : 8'bz;  // Controlled_Buffer controlled_buffer_1
  assign B = A__B ? A : 8'bz;  // Controlled_Buffer controlled_buffer_2
endmodule
